// Digital circuit 1bit-comparator.dig as structural Verilog
module _1bit_comparator (
  input  A,
  input  B,
  input  Higher,
  input  Lower,
  input  Equal
);

  wire xor_1_out;

  xor xor_1 (xor_1_out, A, B);
  and and_1 (Equal, A, B);
  and and_2 (Higher, A, xor_1_out);
  and and_3 (Lower, B, xor_1_out);
endmodule
