// Digital circuit 8bit-adder.dig as structural Verilog
module _8bit_adder (
  input  [7:0] A,
  input  [7:0] B,
  output [7:0] S
);

  wire full_adder_1_cout, full_adder_2_cout, full_adder_3_cout, full_adder_4_cout, full_adder_5_cout,
       full_adder_6_cout, full_adder_7_cout, half_adder_1_cout;

  half_adder half_adder_1 (.A(A[0]), .B(B[0]), .S(S[0]), .Cout(half_adder_1_cout));
  full_adder full_adder_1 (.Cin(half_adder_1_cout), .B(B[1]), .A(A[1]), .Cout(full_adder_1_cout), .S(S[1]));
  full_adder full_adder_2 (.Cin(full_adder_1_cout), .B(B[2]), .A(A[2]), .Cout(full_adder_2_cout), .S(S[2]));
  full_adder full_adder_3 (.Cin(full_adder_2_cout), .B(B[3]), .A(A[3]), .Cout(full_adder_3_cout), .S(S[3]));
  full_adder full_adder_4 (.Cin(full_adder_3_cout), .B(B[4]), .A(A[4]), .Cout(full_adder_4_cout), .S(S[4]));
  full_adder full_adder_5 (.Cin(full_adder_4_cout), .B(B[5]), .A(A[5]), .Cout(full_adder_5_cout), .S(S[5]));
  full_adder full_adder_6 (.Cin(full_adder_5_cout), .B(B[6]), .A(A[6]), .Cout(full_adder_6_cout), .S(S[6]));
  full_adder full_adder_7 (.Cin(full_adder_6_cout), .B(B[7]), .A(A[7]), .Cout(full_adder_7_cout), .S(S[7]));
  // also tied to GND on the sheet: full_adder_7_cout
endmodule
