// Digital circuit 8bit-comparator.dig as structural Verilog
module _8bit_comparator (
  input  [7:0] A,
  input  [7:0] B,
  output gt,
  output eq,
  output lt
);

  wire _4bit_comparator_1_a_eq_b, _4bit_comparator_1_a_gt_b, _4bit_comparator_1_a_lt_b;

  _4bit_comparator _4bit_comparator_1 (
    .A3(A[3]), .B3(B[3]), .A2(A[2]), .B2(B[2]), .CA_lt_B(1'b0), .CA_eq_B(1'b1), .CA_gt_B(1'b0), .A1(A[1]),
    .B1(B[1]), .A0(A[0]), .B0(B[0]), .A_gt_B(_4bit_comparator_1_a_gt_b), .A_eq_B(_4bit_comparator_1_a_eq_b),
    .A_lt_B(_4bit_comparator_1_a_lt_b));
  _4bit_comparator _4bit_comparator_2 (
    .A3(A[7]), .B3(B[7]), .A2(A[6]), .B2(B[6]), .CA_lt_B(_4bit_comparator_1_a_lt_b),
    .CA_eq_B(_4bit_comparator_1_a_eq_b), .CA_gt_B(_4bit_comparator_1_a_gt_b), .A1(A[5]), .B1(B[5]),
    .A0(A[4]), .B0(B[4]), .A_gt_B(gt), .A_eq_B(eq), .A_lt_B(lt));
endmodule
