// Digital circuit 8bit-processor.dig as structural Verilog
module _8bit_processor (
  input  [7:0] A,
  input  [7:0] B,
  input  D,
  input  [3:0] Op,
  output A_gt_B,
  output A_eq_B,
  output A_lt_B
);

  wire button_1_out;
  wire [7:0] _8bit_adder_1_s, _8bit_shifter_1_out, _8bit_subtractor_1_out, multiplexer_1_out,
       multplier_1_out, register_1_o;

  _8bit_adder _8bit_adder_1 (.A(A), .B(B), .S(_8bit_adder_1_s));
  _8bit_subtractor _8bit_subtractor_1 (.A(A), .B(B), .Out(_8bit_subtractor_1_out));
  _8bit_comparator _8bit_comparator_1 (.A(A), .B(B), .gt(A_gt_B), .eq(A_eq_B), .lt(A_lt_B));
  _8bit_shifter _8bit_shifter_1 (.D(D), .A(A), .Out(_8bit_shifter_1_out));
  multplier multplier_1 (.A(A), .B(B), .Out(multplier_1_out));
  Multiplexer #(.Selector_Bits(4), .Bits(8)) multiplexer_1 (
    .sel(Op), .in_0(_8bit_adder_1_s), .in_1(_8bit_subtractor_1_out), .in_2(_8bit_shifter_1_out),
    .in_3(multplier_1_out), .in_4({8{1'b0}}), .in_5({8{1'b0}}), .in_6({8{1'b0}}), .in_7({8{1'b0}}),
    .in_8({8{1'b0}}), .in_9({8{1'b0}}), .in_10({8{1'b0}}), .in_11({8{1'b0}}), .in_12({8{1'b0}}),
    .in_13({8{1'b0}}), .in_14({8{1'b0}}), .in_15({8{1'b0}}), .out(multiplexer_1_out));
  Button button_1 (.out(button_1_out));
  register register_1 (.C(button_1_out), .D(multiplexer_1_out), .O(register_1_o));
  Seven_Seg_Hex seven_seg_hex_1 (.d(register_1_o[7:4]), .dp(1'b0));
  Seven_Seg_Hex seven_seg_hex_2 (.d(register_1_o[3:0]), .dp(1'b0));
endmodule
