// Digital circuit 8bit-shifter.dig as structural Verilog
module _8bit_shifter (
  input  D,
  input  [7:0] A,
  output [7:0] Out
);

  wire and_1_out, and_3_out, and_4_out, and_5_out, and_6_out, and_7_out, and_8_out, and_9_out, and_10_out,
       and_11_out, and_12_out, and_14_out, not_1_out;

  not not_1 (not_1_out, D);
  and and_1 (and_1_out, D, A[0]);
  and and_2 (Out[0], A[1], not_1_out);
  or or_1 (Out[1], and_4_out, and_1_out);
  and and_3 (and_3_out, D, A[1]);
  and and_4 (and_4_out, A[2], not_1_out);
  and and_5 (and_5_out, D, A[2]);
  or or_2 (Out[2], and_6_out, and_3_out);
  and and_6 (and_6_out, A[3], not_1_out);
  or or_3 (Out[3], and_8_out, and_5_out);
  and and_7 (and_7_out, D, A[3]);
  and and_8 (and_8_out, A[4], not_1_out);
  or or_4 (Out[4], and_10_out, and_7_out);
  and and_9 (and_9_out, D, A[4]);
  and and_10 (and_10_out, A[5], not_1_out);
  or or_5 (Out[5], and_12_out, and_9_out);
  and and_11 (and_11_out, D, A[5]);
  and and_12 (and_12_out, A[6], not_1_out);
  or or_6 (Out[6], and_14_out, and_11_out);
  and and_13 (Out[7], D, A[6]);
  and and_14 (and_14_out, A[7], not_1_out);
endmodule
