// Digital circuit 8bit-subtractor.dig as structural Verilog
module _8bit_subtractor (
  input  [7:0] A,
  input  [7:0] B,
  output [7:0] Out
);

  wire full_subtractor_1_bout, full_subtractor_2_bout, full_subtractor_3_bout, full_subtractor_4_bout,
       full_subtractor_5_bout, full_subtractor_6_bout, full_subtractor_7_bout, half_subtractor_1_bor;

  half_subtractor half_subtractor_1 (.A(A[0]), .B(B[0]), .Dif(Out[0]), .Bor(half_subtractor_1_bor));
  full_subtractor full_subtractor_1 (
    .A(A[1]), .B(B[1]), .Bin(half_subtractor_1_bor), .Dif(Out[1]), .Bout(full_subtractor_1_bout));
  full_subtractor full_subtractor_2 (
    .A(A[2]), .B(B[2]), .Bin(full_subtractor_1_bout), .Dif(Out[2]), .Bout(full_subtractor_2_bout));
  full_subtractor full_subtractor_3 (
    .A(A[3]), .B(B[3]), .Bin(full_subtractor_2_bout), .Dif(Out[3]), .Bout(full_subtractor_3_bout));
  full_subtractor full_subtractor_4 (
    .A(A[4]), .B(B[4]), .Bin(full_subtractor_3_bout), .Dif(Out[4]), .Bout(full_subtractor_4_bout));
  full_subtractor full_subtractor_5 (
    .A(A[5]), .B(B[5]), .Bin(full_subtractor_4_bout), .Dif(Out[5]), .Bout(full_subtractor_5_bout));
  full_subtractor full_subtractor_6 (
    .A(A[6]), .B(B[6]), .Bin(full_subtractor_5_bout), .Dif(Out[6]), .Bout(full_subtractor_6_bout));
  full_subtractor full_subtractor_7 (
    .A(A[7]), .B(B[7]), .Bin(full_subtractor_6_bout), .Dif(Out[7]), .Bout(full_subtractor_7_bout));
  // also tied to GND on the sheet: full_subtractor_7_bout
endmodule
