// Digital circuit full-subtractor.dig as structural Verilog
module full_subtractor (
  input  A,
  input  B,
  input  Bin,
  output Dif,
  output Bout
);

  wire half_subtractor_1_bor, half_subtractor_1_dif, half_subtractor_2_bor;

  half_subtractor half_subtractor_1 (.A(A), .B(B), .Dif(half_subtractor_1_dif), .Bor(half_subtractor_1_bor));
  half_subtractor half_subtractor_2 (.A(half_subtractor_1_dif), .B(Bin), .Dif(Dif), .Bor(half_subtractor_2_bor));
  or or_1 (Bout, half_subtractor_2_bor, half_subtractor_1_bor);
endmodule
