// Digital circuit half-subtractor.dig as structural Verilog
module half_subtractor (
  input  A,
  input  B,
  output Dif,
  output Bor
);

  wire not_1_out;

  not not_1 (not_1_out, A);
  xor xor_1 (Dif, A, B);
  and and_1 (Bor, B, not_1_out);
endmodule
