// Digital circuit multiplexer.dig as structural Verilog
module multiplexer (
  input  D0,
  input  D1,
  input  D2,
  input  D3,
  input  D4,
  input  D5,
  input  D6,
  input  D7,
  input  [2:0] In,
  output Out
);

  wire and_1_out, and_2_out, and_3_out, and_4_out, and_5_out, and_6_out, and_7_out, and_8_out, not_1_out,
       not_2_out, not_3_out;

  not not_1 (not_1_out, In[2]);
  not not_2 (not_2_out, In[1]);
  not not_3 (not_3_out, In[0]);
  and and_1 (and_1_out, D0, not_1_out, not_2_out, not_3_out);
  and and_2 (and_2_out, D1, not_1_out, not_2_out, In[0]);
  and and_3 (and_3_out, D2, not_1_out, not_3_out, In[1]);
  and and_4 (and_4_out, D3, not_1_out, In[1], In[0]);
  and and_5 (and_5_out, D4, In[2], not_2_out, not_3_out);
  and and_6 (and_6_out, D5, In[2], not_2_out, In[0]);
  and and_7 (and_7_out, D6, In[2], In[1], not_3_out);
  and and_8 (and_8_out, D7, In[2], In[1], In[0]);
  or or_1 (Out, and_1_out, and_2_out, and_3_out, and_4_out, and_5_out, and_6_out, and_7_out, and_8_out);
endmodule
