// Digital circuit multplier.dig as structural Verilog
module multplier (
  input  [7:0] A,
  input  [7:0] B,
  output [7:0] Out
);

  wire and_1_out, and_2_out, and_3_out, and_4_out, and_5_out, and_6_out, and_7_out, and_8_out, and_9_out,
       and_10_out, and_11_out, and_12_out, and_13_out, and_14_out, and_15_out, full_adder_2_cout,
       full_adder_2_s, full_adder_3_cout, full_adder_4_cout, full_adder_4_s, full_adder_5_cout,
       full_adder_5_s, full_adder_6_cout, full_adder_7_cout, full_adder_7_s, full_adder_8_cout,
       full_adder_8_s, full_adder_9_cout, full_adder_10_cout, full_adder_10_s, full_adder_11_cout,
       full_adder_12_cout;

  full_adder full_adder_1 (.Cin(full_adder_3_cout), .B(and_2_out), .A(full_adder_2_cout), .Cout(Out[7]), .S(Out[6]));
  and and_1 (and_1_out, A[3], B[1]);
  and and_2 (and_2_out, A[3], B[3]);
  full_adder full_adder_2 (
    .Cin(full_adder_5_cout), .B(and_4_out), .A(full_adder_4_cout), .Cout(full_adder_2_cout),
    .S(full_adder_2_s));
  full_adder full_adder_3 (
    .Cin(full_adder_6_cout), .B(and_5_out), .A(full_adder_2_s), .Cout(full_adder_3_cout), .S(Out[5]));
  and and_3 (and_3_out, A[2], B[1]);
  full_adder full_adder_4 (
    .Cin(full_adder_7_cout), .B(and_1_out), .A(1'b0), .Cout(full_adder_4_cout), .S(full_adder_4_s));
  and and_4 (and_4_out, A[3], B[2]);
  and and_5 (and_5_out, A[2], B[3]);
  and and_6 (and_6_out, A[3], B[0]);
  full_adder full_adder_5 (
    .Cin(full_adder_8_cout), .B(and_8_out), .A(full_adder_4_s), .Cout(full_adder_5_cout), .S(full_adder_5_s));
  and and_7 (and_7_out, A[1], B[3]);
  full_adder full_adder_6 (
    .Cin(full_adder_9_cout), .B(and_7_out), .A(full_adder_5_s), .Cout(full_adder_6_cout), .S(Out[4]));
  full_adder full_adder_7 (
    .Cin(full_adder_10_cout), .B(and_3_out), .A(and_6_out), .Cout(full_adder_7_cout), .S(full_adder_7_s));
  and and_8 (and_8_out, A[2], B[2]);
  and and_9 (and_9_out, A[1], B[1]);
  and and_10 (and_10_out, A[1], B[2]);
  full_adder full_adder_8 (
    .Cin(full_adder_11_cout), .B(and_10_out), .A(full_adder_7_s), .Cout(full_adder_8_cout), .S(full_adder_8_s));
  and and_11 (and_11_out, A[0], B[3]);
  full_adder full_adder_9 (.Cin(1'b0), .B(and_11_out), .A(full_adder_8_s), .Cout(full_adder_9_cout), .S(Out[3]));
  and and_12 (and_12_out, A[2], B[0]);
  full_adder full_adder_10 (
    .Cin(full_adder_12_cout), .B(and_9_out), .A(and_12_out), .Cout(full_adder_10_cout), .S(full_adder_10_s));
  and and_13 (and_13_out, A[0], B[2]);
  full_adder full_adder_11 (.Cin(1'b0), .B(and_13_out), .A(full_adder_10_s), .Cout(full_adder_11_cout), .S(Out[2]));
  and and_14 (and_14_out, A[0], B[1]);
  and and_15 (and_15_out, A[1], B[0]);
  full_adder full_adder_12 (.Cin(1'b0), .B(and_14_out), .A(and_15_out), .Cout(full_adder_12_cout), .S(Out[1]));
  and and_16 (Out[0], A[0], B[0]);

  assign A[6:4] = {3{A[7]}};
  assign B[6:4] = {3{B[7]}};
  // also tied to GND on the sheet: {A[7], B[7]}
endmodule
