// Digital circuit register.dig as structural Verilog
module register (
  input  C,
  input  [7:0] D,
  output [7:0] O
);

  D_FF d_ff_1 (.D(D[0]), .C(C), .Q(O[0]));  // open: nQ
  D_FF d_ff_2 (.D(D[1]), .C(C), .Q(O[1]));  // open: nQ
  D_FF d_ff_3 (.D(D[2]), .C(C), .Q(O[2]));  // open: nQ
  D_FF d_ff_4 (.D(D[3]), .C(C), .Q(O[3]));  // open: nQ
  D_FF d_ff_5 (.D(D[4]), .C(C), .Q(O[4]));  // open: nQ
  D_FF d_ff_6 (.D(D[5]), .C(C), .Q(O[5]));  // open: nQ
  D_FF d_ff_7 (.D(D[6]), .C(C), .Q(O[6]));  // open: nQ
  D_FF d_ff_8 (.D(D[7]), .C(C), .Q(O[7]));  // open: nQ
endmodule
